# Fritzing sketch 02_8Led (saved by Fritzing 0.8.7b)
breadboards: 1

parts:
  Raspberry_Pi_B_rev1 = Raspberry Pi B rev2
  R2 = Resistor [tolerance=±5% resistance=220 package=THT]
  LED1 = LED - 5mm [color="Red (633nm)" package="5 mm [THT]"]
  LED2 = LED - 5mm [color="Red (633nm)" package="5 mm [THT]"]
  LED3 = LED - 5mm [color="Red (633nm)" package="5 mm [THT]"]
  LED4 = LED - 5mm [color="Red (633nm)" package="5 mm [THT]"]
  LED5 = LED - 5mm [color="Red (633nm)" package="5 mm [THT]"]
  LED6 = LED - 5mm [color="Red (633nm)" package="5 mm [THT]"]
  LED7 = LED - 5mm [color="Red (633nm)" package="5 mm [THT]"]
  LED8 = LED - 5mm [color="Red (633nm)" package="5 mm [THT]"]
  R3 = Resistor [tolerance=±5% resistance=220 package=THT]
  R4 = Resistor [tolerance=±5% resistance=220 package=THT]
  R5 = Resistor [tolerance=±5% resistance=220 package=THT]
  R6 = Resistor [tolerance=±5% resistance=220 package=THT]
  R7 = Resistor [package="2010 [SMD]"]
  R8 = Resistor [tolerance=±5% resistance=220 package=THT]
  R9 = Resistor [package="2010 [SMD]"]

nets:
  N1: Raspberry_Pi_B_rev1.5V, R2.Pin_0, R3.Pin_1, R4.Pin_1, R5.Pin_1, R6.Pin_1, R7.Pin_1, R8.Pin_1, R9.Pin_1
  N2: Raspberry_Pi_B_rev1.GPIO_23, LED7.cathode
  N3: Raspberry_Pi_B_rev1.GPIO_17, LED1.cathode
  N4: Raspberry_Pi_B_rev1.GPIO_18, LED2.cathode
  N5: Raspberry_Pi_B_rev1.GPIO_27, LED3.cathode
  N6: Raspberry_Pi_B_rev1.GPIO_22, LED4.cathode
  N7: Raspberry_Pi_B_rev1.GPIO_4, LED6.cathode
  N8: Raspberry_Pi_B_rev1.GPIO_24, LED8.cathode
  N9: Raspberry_Pi_B_rev1.GPIO_25, LED5.cathode
  N10: R2.Pin_1, LED1.anode
  N11: LED2.anode, R3.Pin_0
  N12: LED3.anode, R4.Pin_0
  N13: LED4.anode, R6.Pin_0
  N14: LED5.anode, R9.Pin_0
  N15: LED6.anode, R8.Pin_0
  N16: LED7.anode, R5.Pin_0
  N17: LED8.anode, R7.Pin_0
