# Fritzing sketch 03_btnAndLed (saved by Fritzing 0.8.7b)
breadboards: 1

parts:
  Raspberry_Pi_B_rev1 = Raspberry Pi B rev2
  R2 = Resistor [tolerance=±5% resistance=220 package=THT]
  LED1 = LED - 5mm [color="Red (633nm)" package="5 mm [THT]"]
  S1 = Pushbutton [package="[THT]"]

nets:
  N1: Raspberry_Pi_B_rev1.5V, R2.Pin_1
  N2: Raspberry_Pi_B_rev1.GND, S1.Pin_3, S1.Pin_4
  N3: Raspberry_Pi_B_rev1.GPIO_17, LED1.cathode
  N4: Raspberry_Pi_B_rev1.GPIO_18, S1.Pin_1, S1.Pin_2
  N5: R2.Pin_0, LED1.anode
