# Fritzing sketch Tilt Switch (saved by Fritzing 0.9.1b)
breadboards: 1

parts:
  Raspberry_Pi1 = Raspberry Pi B rev2
  LED1 = LED - 5mm [color="Red (633nm)" package="5 mm [THT]"]
  R1 = Resistor [tolerance=±5% resistance=4.7k package="0805 [SMD]"]
  S1 = Tilt Switch [package=THT]

nets:
  N1: Raspberry_Pi1.5V, R1.Pin_1
  N2: Raspberry_Pi1.GND, S1.Pin_1
  N3: Raspberry_Pi1.GPIO_17, LED1.cathode
  N4: Raspberry_Pi1.GPIO_18, S1.Pin_2
  N5: LED1.anode, R1.Pin_0

notes:
  PC0
  PC1
  PC2
  PC3
  PC4
  PC5
  PC6
  PC7
  TXD
  CE0
  MOSI
  RXD
  SCL
  SCLK
  CE1
  MISO
  SCA
