# Fritzing sketch 05_Beep (saved by Fritzing 0.8.7b)
breadboards: 1

parts:
  Raspberry_Pi_B_rev1 = Raspberry Pi B rev2
  R2 = Resistor [tolerance=±5% resistance=220 package=THT]
  J1 = Piezo Speaker
  Q1 = PNP-Transistor [package="SOT-23 [SMD]"]

nets:
  N1: Raspberry_Pi_B_rev1.5V, J1.pin2
  N2: Raspberry_Pi_B_rev1.GPIO_17, R2.Pin_1
  N3: Raspberry_Pi_B_rev1.GND, Q1.1
  N4: R2.Pin_0, Q1.0
  N5: J1.pin1, Q1.2
