# Fritzing sketch 06_RGB (saved by Fritzing 0.8.7b)
breadboards: 1

parts:
  Raspberry_Pi_B_rev1 = Raspberry Pi B rev2
  R2 = Resistor [tolerance=±5% resistance=220 package=THT]
  R3 = Resistor [tolerance=±5% resistance=220 package=THT]
  R4 = Resistor [tolerance=±5% resistance=220 package=THT]
  LED1 = RGB LED (com. cathode, rgb) [package="5 mm [THT]"]

nets:
  N1: Raspberry_Pi_B_rev1.GND, LED1.common_cathode
  N2: Raspberry_Pi_B_rev1.GPIO_17, R2.Pin_0
  N3: Raspberry_Pi_B_rev1.GPIO_18, R3.Pin_0
  N4: Raspberry_Pi_B_rev1.GPIO_27, R4.Pin_0
  N5: R2.Pin_1, LED1.red_anode
  N6: R3.Pin_1, LED1.green_anode
  N7: R4.Pin_1, LED1.blue_anode
