# Fritzing sketch 08_relay (saved by Fritzing 0.8.7b)
breadboards: 1

parts:
  Raspberry_Pi_B_rev1 = Raspberry Pi B rev2
  R2 = Resistor [tolerance=±5% resistance=220 package=THT]
  Q1 = PNP-Transistor [package="SOT-23 [SMD]"]
  K1 = Relay [part_number=FRS1B-S package=THT]
  D1 = Rectifier Diode [part_number=1N4001 package="300 mil [THT]"]

nets:
  N1: Raspberry_Pi_B_rev1.5V, K1.COIL2, D1.cathode
  N2: Raspberry_Pi_B_rev1.GPIO_17, R2.Pin_1
  N3: Raspberry_Pi_B_rev1.GND, Q1.1
  N4: R2.Pin_0, Q1.0
  N5: Q1.2, K1.COIL1
  N6: K1.C1, K1.C2
