# Fritzing sketch Relay (saved by Fritzing 0.9.1b)
breadboards: 1

parts:
  Raspberry_Pi1 = Raspberry Pi B rev2
  Q2 = PNP-Transistor [package="SOT-23 [SMD]"]
  K2 = Relay [part_number=FRS1B-S package=THT]
  R3 = Resistor [tolerance=±5% resistance=1k package=THT]
  D2 = Rectifier Diode [part_number=1N4001 package="300 mil [THT]"]

nets:
  N1: Raspberry_Pi1.5V, D2.cathode
  N2: Raspberry_Pi1.GND, Q2.1
  N3: Raspberry_Pi1.GPIO_17, R3.Pin_1
  N4: Q2.0, R3.Pin_0
  N5: K2.A, K2.COIL1, D2.anode
  N6: K2.C1, K2.C2
  N7: K2.COIL2, K2.B

notes:
  PC0
  PC1
  PC2
  PC3
  PC4
  PC5
  PC6
  PC7
  TXD
  CE0
  MOSI
  RXD
  SCL
  SCLK
  CE1
  MISO
  SCA
