# Fritzing sketch 10_servo (saved by Fritzing 0.8.7b)

parts:
  Raspberry_Pi_B_rev1 = Raspberry Pi B rev2
  J1 = Basic Servo

nets:
  5V: Raspberry_Pi_B_rev1.5V, J1.vcc
  GND: Raspberry_Pi_B_rev1.GND, J1.gnd
  N1: Raspberry_Pi_B_rev1.GPIO_17, J1.pulse
